// Digital circuit cpu.dig as structural Verilog
module cpu (
  input  [1:0] nextpc,
  input  Clk,
  output [31:0] out_1
);

  wire [1:0] PC_q;

  Register #(.Bits(2)) PC (.D(nextpc), .en(1'b1), .Q(PC_q));  // open: C
  ROM #(.Bits(32)) ProgMem (.A(PC_q), .sel(1'b1), .D(out_1));

  // Notes on the sheet:
  //   contents of ProgMem (hex, n*v repeats v):
  //   1d90db3,5146b3
endmodule
