// Digital circuit multiplexor.dig as structural Verilog
module multiplexor (
  input  [3:0] Input_0,
  input  [3:0] Input_1,
  input  ctrl,
  output [3:0] Output
);

  // Probe on Input_0
  // Probe on Input_1
  Multiplexer #(.Bits(4)) multiplexer_1 (.sel(ctrl), .in_0(Input_0), .in_1(Input_1), .out(Output));
  // Probe on Output
endmodule
