// Digital circuit record.dig as structural Verilog
module record (
  input  [3:0] Data,
  input  Clk,
  input  en,
  output [3:0] out_4
);

  // Probe on Data
  // Probe on en
  Register #(.Bits(4)) register_1 (.D(Data), .C(Clk), .en(en), .Q(out_4));
  // Probe on out_4
endmodule
