// Digital circuit ru.dig as structural Verilog
module ru (
  input  clk,
  input  [1:0] rs1,
  input  [1:0] rs2,
  input  [1:0] rd,
  input  [31:0] data,
  output [31:0] rs1_data,
  output [31:0] rs2_data
);

  wire en0, en1, en2, en3;
  wire [31:0] x0, x1, x2, x3;

  Decoder #(.Selector_Bits(2)) decoder_1 (.sel(rd), .out_0(en0), .out_1(en1), .out_2(en2), .out_3(en3));
  Register #(.Bits(32)) u_x0 (.D({32{1'b0}}), .C(clk), .en(en0), .Q(x0));
  Register #(.Bits(32)) u_x1 (.D(data), .C(clk), .en(en1), .Q(x1));
  Register #(.Bits(32)) u_x2 (.D(data), .C(clk), .en(en2), .Q(x2));
  Register #(.Bits(32)) u_x3 (.D(data), .C(clk), .en(en3), .Q(x3));
  Multiplexer #(.Selector_Bits(2), .Bits(32)) multiplexer_1 (
    .sel(rs1), .in_0(x0), .in_1(x1), .in_2(x2), .in_3(x3), .out(rs1_data));
  Multiplexer #(.Selector_Bits(2), .Bits(32)) multiplexer_2 (
    .sel(rs2), .in_0(x0), .in_1(x1), .in_2(x2), .in_3(x3), .out(rs2_data));
endmodule
