// Digital circuit simple_record.dig as structural Verilog
module simple_record (
  input  Data,
  input  Clk,
  input  en,
  output out_4
);

  // Probe on Data
  // Probe on en
  Register register_1 (.D(Data), .C(Clk), .en(en), .Q(out_4));
  // Probe on out_4
endmodule
